# Fritzing sketch proto (saved by Fritzing 0.9.3b)
breadboards: 1

parts:
  Raspberry_Pi_1 = Raspberry Pi 3 [part_number=RPI-3-V1.2]
  DHT1 = DHT11 Humitidy and Temperature Sensor
  YL-83_-_Control_Board1 = YL-83 Rain Sensor - Control Board
  YL-83_-_Detection_Board1 = YL-83 Rain Sensor - Detection Board
  R1 = Resistor [tolerance=±5% resistance=220 package=THT]
  R2 = Resistor [tolerance=±5% resistance=220 package=THT]

nets:
  3V3: Raspberry_Pi_1.3V3, DHT1.VDD, YL-83_-_Control_Board1.VCC, R1.Pin_1, R2.Pin_0
  N1: Raspberry_Pi_1.GIPO9, DHT1.DATA, R1.Pin_0
  N2: Raspberry_Pi_1.GIPO11, YL-83_-_Control_Board1.DO, R2.Pin_1
  GND: Raspberry_Pi_1.GND, DHT1.GND, YL-83_-_Control_Board1.GND
  N3: YL-83_-_Control_Board1.POS, YL-83_-_Detection_Board1.POS
  N4: YL-83_-_Control_Board1.NEG, YL-83_-_Detection_Board1.NEG

custom parts:
  DHT11 Humitidy and Temperature Sensor: DHT11 Humidity and Temperature Sensor
  YL-83 Rain Sensor - Control Board: The YL-83 is a rain sensor that has more resistance when dry and less resistance when wet. The module runs at 5V.
  YL-83 Rain Sensor - Detection Board: The YL-83 is a rain sensor that has more resistance when dry and less resistance when wet. The module runs at 5V.
